# Fritzing sketch FishFeeder (saved by Fritzing 0.9.3b)
breadboards: 1

parts:
  S1 = Round Pushbutton
  Part1 = Arduino Uno (Rev3) - ICSP
  J1 = Basic Servo
  U1 = LCD-16X2 [package=lcd-16x2_noholes]  # not connected
  U2 = POT [package=pot_mammoth]
  R1 = Resistor [tolerance=±5% resistance=220 package="0805 [SMD]"]

nets:
  N1: S1.leg0, Part1.D7
  GND: S1.leg1, Part1.D12/MISO, Part1.GND, J1.gnd, U2.E
  5V: Part1.5V, J1.vcc, U2.S, R1.Pin_0
  N2: Part1.D9_PWM, J1.pulse
