# Fritzing sketch tempDetector (saved by Fritzing 0.9.3b)
breadboards: 1

parts:
  U1 = TMP36 [package=to-92]
  Part1 = Arduino Uno (Rev3) - ICSP
  LED1 = smd LED [color="Red (633nm)" package="0805 [SMD]"]
  LED2 = smd LED [color="Yellow (595nm)" package="0805 [SMD]"]
  LED3 = smd LED [color="White (6500K)" package="0805 [SMD]"]
  LED4 = smd LED [color="Green (565nm)" package="0805 [SMD]"]
  LED5 = smd LED [color="Blue (430nm)" package="0805 [SMD]"]
  R6 = Resistor [tolerance=±5% resistance=220 package="2512 [SMD]"]  # not connected
  R7 = Resistor [tolerance=±5% resistance=220 package=THT]
  R8 = Resistor [tolerance=±5% resistance=220 package=THT]
  R9 = Resistor [tolerance=±5% resistance=220 package=THT]
  R10 = Resistor [tolerance=±5% resistance=220 package=THT]
  R11 = Resistor [tolerance=±5% resistance=220 package=THT]

nets:
  VCC: U1.VCC, Part1.5V
  N1: U1.VOUT, Part1.A1
  GND: U1.GND, Part1.GND, R7.Pin_0, R8.Pin_0, R9.Pin_0, R10.Pin_0, R11.Pin_0
  N2: Part1.D2, LED1.anode
  N3: Part1.D3_PWM, LED2.anode
  N4: Part1.D4, LED3.anode
  N5: Part1.D5_PWM, LED4.anode
  N6: Part1.D6_PWM, LED5.anode
  N7: LED1.cathode, R7.Pin_1
  N8: LED2.cathode, R8.Pin_1
  N9: LED3.cathode, R9.Pin_1
  N10: LED4.cathode, R10.Pin_1
  N11: LED5.cathode, R11.Pin_1
